# Fritzing sketch IC_Motor (saved by Fritzing 0.9.3b)
breadboards: 1

parts:
  Part2 = Arduino Uno (Rev3)
  IC1 = L293D [package=THT]
  VCC1 = Battery
  M1 = DC Motor
  M2 = DC Motor

nets:
  N1: Part2.D9_PWM, IC1.Enable_1
  N2: Part2.D10_PWM/SS, IC1.In_1
  N3: Part2.D11_PWM/MOSI, IC1.In_2
  N4: Part2.GND, IC1.0V, VCC1.-
  N5: Part2.D3_PWM, IC1.Enable_2
  N6: Part2.D4, IC1.In_4
  N7: Part2.D5_PWM, IC1.In_3
  N8: Part2.5V, IC1.+V
  N9: IC1.Out_1_(_Controlled_by_Enable_1_), M2.pin_2
  N10: IC1.Out_2_(_Controlled_by_Enable_1_), M2.pin_1
  N11: IC1.+Vmotor, VCC1.+
  N12: IC1.Out_3_(_Controlled_by_Enable_2_), M1.pin_2
  N13: IC1.Out_4_(_Controlled_by_Enable_2_), M1.pin_1
